# Fritzing sketch Frizzing_Arduino_SpikeNetwork (saved by Fritzing 0.9.3b)
breadboards: 2

parts:
  Componente1 = Arduino Uno (Rev3)
  R1 = Rotary Potentiometer (Small) [maximum_resistance=100kΩ package=THT]
  LED1 = LED - 5mm [color="Green (565nm)" package="5 mm [THT]"]
  Bottone_Potenziometro = Pushbutton [package="[THT]"]
  Bottone_Modalità = Pushbutton [package="[THT]"]
  Buzzer_-_Spike = Piezo Speaker
  LED2 = LED - 5mm [color="Red (633nm)" package="5 mm [THT]"]
  R2 = Resistor [tolerance=±5% resistance=10 package=THT]
  R3 = Resistor [tolerance=±5% resistance=10 package=THT]
  R4 = Resistor [tolerance=±5% resistance=10 package=THT]
  R5 = Resistor [tolerance=±5% resistance=10 package=THT]
  Componente2 = Arduino Uno (Rev3)
  LED3 = LED - 5mm [color="Red (633nm)" package="5 mm [THT]"]
  R6 = Resistor [tolerance=±5% resistance=10 package=THT]
  S1 = Pushbutton [package="[THT]"]
  R7 = Resistor [tolerance=±5% resistance=10 package=THT]
  S2 = Pushbutton [package="[THT]"]
  R8 = Resistor [tolerance=±5% resistance=10 package=THT]
  Buzzer_-_Spike1 = Piezo Speaker

nets:
  N1: Componente1.A0, R1.wiper
  N2: Componente1.D8, Componente2.D2, LED3.anode
  N3: Componente1.D2, Bottone_Modalità.Pin_3, Bottone_Modalità.Pin_4, R2.Pin_1
  N4: Componente1.D4, Buzzer_-_Spike.pin2
  N5: Componente1.D5_PWM, R4.Pin_0
  N6: Componente1.D6_PWM, Bottone_Potenziometro.Pin_3, Bottone_Potenziometro.Pin_4, R3.Pin_1
  N7: Componente1.D7, R5.Pin_0
  N8: Componente1.5V, R1.leg2, Bottone_Potenziometro.Pin_1, Bottone_Potenziometro.Pin_2, Bottone_Modalità.Pin_1, Bottone_Modalità.Pin_2
  N9: Componente1.GND, R1.leg1, LED1.cathode, Buzzer_-_Spike.pin1, LED2.cathode, R2.Pin_0, R3.Pin_0
  N10: LED1.anode, R5.Pin_1
  N11: LED2.anode, R4.Pin_1
  N12: Componente2.D4, S1.Pin_3, S1.Pin_4, R7.Pin_1
  N13: Componente2.D6_PWM, S2.Pin_3, S2.Pin_4, R8.Pin_1
  N14: Componente2.D7, Buzzer_-_Spike1.pin2
  N15: Componente2.5V, S1.Pin_1, S1.Pin_2, S2.Pin_1, S2.Pin_2
  N16: Componente2.GND, R6.Pin_1, R7.Pin_0, R8.Pin_0, Buzzer_-_Spike1.pin1
  N17: LED3.cathode, R6.Pin_0
