# Fritzing sketch Frizzing_Arduino_Spike (saved by Fritzing 0.9.3b)
breadboards: 1

parts:
  Componente1 = Arduino Uno (Rev3)
  R1 = Rotary Potentiometer (Small) [maximum_resistance=100kΩ package=THT]
  LED1 = LED - 5mm [color="Green (565nm)" package="5 mm [THT]"]
  Bottone_Potenziometro = Pushbutton [package="[THT]"]
  Bottone_Modalità = Pushbutton [package="[THT]"]
  Buzzer_-_Spike = Piezo Speaker
  LED2 = LED - 5mm [color="Red (633nm)" package="5 mm [THT]"]
  R2 = Resistor [tolerance=±5% resistance=10 package=THT]
  R3 = Resistor [tolerance=±5% resistance=10 package=THT]
  R4 = Resistor [tolerance=±5% resistance=10 package=THT]
  R5 = Resistor [tolerance=±5% resistance=10 package=THT]

nets:
  N1: Componente1.A0, R1.wiper
  N2: Componente1.D2, Bottone_Modalità.Pin_3, Bottone_Modalità.Pin_4, R2.Pin_1
  N3: Componente1.D4, Buzzer_-_Spike.pin2
  N4: Componente1.D5_PWM, R4.Pin_0
  N5: Componente1.D6_PWM, Bottone_Potenziometro.Pin_3, Bottone_Potenziometro.Pin_4, R3.Pin_1
  N6: Componente1.D7, R5.Pin_0
  N7: Componente1.5V, R1.leg2
  N8: Componente1.GND, R1.leg1, LED1.cathode, Bottone_Potenziometro.Pin_1, Bottone_Potenziometro.Pin_2, Bottone_Modalità.Pin_1, Bottone_Modalità.Pin_2, Buzzer_-_Spike.pin1, LED2.cathode, R2.Pin_0, R3.Pin_0
  N9: LED1.anode, R5.Pin_1
  N10: LED2.anode, R4.Pin_1
